// Digital circuit 1_tres_estados_1bit.dig as structural Verilog
module _1_tres_estados_1bit (
  input  A,
  input  A_en,
  input  B,
  input  B_en,
  input  C,
  input  C_en,
  output Res
);

  assign Res = A_en ? A : 1'bz;  // Driver driver_1
  assign Res = B_en ? B : 1'bz;  // Driver driver_2
  assign Res = C_en ? C : 1'bz;  // Driver driver_3

  // Notes on the sheet:
  //   1) Componentes de 3 estados - bus de salida
endmodule
