// Digital circuit 2a_reg_salida_restringida_1bit.dig as structural Verilog
module _2a_reg_salida_restringida_1bit (
  input  in,
  input  clk,
  input  en_out,
  input  W,
  output out_d,
  output out
);

  wire and_1_out;

  and and_1 (and_1_out, W, clk);
  D_FF d_ff_1 (.D(in), .C(and_1_out), .Q(out_d));  // open: nQ
  assign out = en_out ? out_d : 1'bz;  // Driver driver_1

  // Notes on the sheet:
  //   2a) Registro de salida restringida - 1 bit
  //   salida de debug
endmodule
