// Digital circuit 2b_transferencia_registros.dig as structural Verilog
module _2b_transferencia_registros (
  input  clk,
  input  en0,
  input  en1,
  input  en2,
  input  W0,
  input  W1,
  input  W2,
  input  force_input,
  input  en_force_input,
  output BUS,
  output R0,
  output R1,
  output R2
);

  assign BUS = en_force_input ? force_input : 1'bz;  // Driver driver_1
  _2a_reg_salida_restringida_1bit _2a_reg_salida_restringida_1bit_1 (
    .in(BUS), .clk(clk), .en_out(en0), .W(W0), .out_d(R0), .out(BUS));
  _2a_reg_salida_restringida_1bit _2a_reg_salida_restringida_1bit_2 (
    .in(BUS), .clk(clk), .en_out(en1), .W(W1), .out_d(R1), .out(BUS));
  _2a_reg_salida_restringida_1bit _2a_reg_salida_restringida_1bit_3 (
    .in(BUS), .clk(clk), .en_out(en2), .W(W2), .out_d(R2), .out(BUS));

  // Notes on the sheet:
  //   2b) Secuencia de transferencia entre registros - 1 bit
endmodule
