// Digital circuit 3a_reg_salida_restringida_4bits.dig as structural Verilog
module _3a_reg_salida_restringida_4bits (
  input  clk,
  input  [7:0] IN_8,
  input  en_o,
  input  W,
  output [7:0] out_d,
  output [7:0] out
);

  _2a_reg_salida_restringida_1bit _2a_reg_salida_restringida_1bit_1 (
    .in(IN_8[0]), .clk(clk), .en_out(en_o), .W(W), .out_d(out_d[0]), .out(out[0]));
  _2a_reg_salida_restringida_1bit _2a_reg_salida_restringida_1bit_2 (
    .in(IN_8[1]), .clk(clk), .en_out(en_o), .W(W), .out_d(out_d[1]), .out(out[2]));
  _2a_reg_salida_restringida_1bit _2a_reg_salida_restringida_1bit_3 (
    .in(IN_8[2]), .clk(clk), .en_out(en_o), .W(W), .out_d(out_d[2]), .out(out[1]));
  _2a_reg_salida_restringida_1bit _2a_reg_salida_restringida_1bit_4 (
    .in(IN_8[3]), .clk(clk), .en_out(en_o), .W(W), .out_d(out_d[3]), .out(out[3]));
  _2a_reg_salida_restringida_1bit _2a_reg_salida_restringida_1bit_5 (
    .in(IN_8[4]), .clk(clk), .en_out(en_o), .W(W), .out_d(out_d[4]), .out(out[4]));
  _2a_reg_salida_restringida_1bit _2a_reg_salida_restringida_1bit_6 (
    .in(IN_8[5]), .clk(clk), .en_out(en_o), .W(W), .out_d(out_d[5]), .out(out[5]));
  _2a_reg_salida_restringida_1bit _2a_reg_salida_restringida_1bit_7 (
    .in(IN_8[6]), .clk(clk), .en_out(en_o), .W(W), .out_d(out_d[6]), .out(out[6]));
  _2a_reg_salida_restringida_1bit _2a_reg_salida_restringida_1bit_8 (
    .in(IN_8[7]), .clk(clk), .en_out(en_o), .W(W), .out_d(out_d[7]), .out(out[7]));

  // Other names for the same wires on the sheet: en = en_o

  // Notes on the sheet:
  //   habilitación de salida
  //   3a) Registro salida restringida - 8 bit
  //   salida de debug
endmodule
