// Digital circuit 3a_reg_salida_restringida_8bits.dig as structural Verilog
module _3a_reg_salida_restringida_8bits (
  input  clk,
  input  [7:0] IN_8,
  input  en_o,
  input  W,
  output [7:0] out_d,
  output [7:0] out
);

  _3a_reg_salida_restringida_4bits _3a_reg_salida_restringida_4bits_1 (
    .clk(clk), .IN_4(IN_8[3:0]), .en_o(en_o), .W(W), .out_d(out_d[3:0]), .out(out[3:0]));
  _3a_reg_salida_restringida_4bits _3a_reg_salida_restringida_4bits_2 (
    .clk(clk), .IN_4(IN_8[7:4]), .en_o(en_o), .W(W), .out_d(out_d[7:4]), .out(out[7:4]));
endmodule
