// Digital circuit 3b_ALU_registros_4bits.dig as structural Verilog
module _3b_ALU_registros_4bits (
  input  clk,
  input  [7:0] A,
  input  [7:0] B,
  input  Write_A,
  input  Write_B,
  input  [2:0] OP,
  input  en_out,
  output [7:0] a_2,
  output [7:0] b_2,
  output [7:0] S_debug,
  output [7:0] S,
  output C,
  output Z,
  output N,
  output V
);

  wire not_1_out, notconnected_1_out, notconnected_2_out, notconnected_3_out;
  wire [7:0] A_t, alu_completa_t_1_s, B_t;

  _3a_reg_salida_restringida_8bits _3a_reg_salida_restringida_8bits_1 (
    .clk(clk), .IN_8(A), .en_o(1'b1), .W(Write_A), .out_d(a_2), .out(A_t));
  _3a_reg_salida_restringida_8bits _3a_reg_salida_restringida_8bits_2 (
    .clk(clk), .IN_8(B), .en_o(1'b1), .W(Write_B), .out_d(b_2), .out(B_t));
  Seven_Seg_Hex seven_seg_hex_1 (.d(a_2[7:4]), .dp(notconnected_1_out));
  Seven_Seg_Hex seven_seg_hex_2 (.d(a_2[3:0]), .dp(notconnected_1_out));
  // NotConnected on notconnected_1_out
  ALU_completa_t alu_completa_t_1 (.A(A_t), .B(B_t), .OP(OP), .C(C), .Z(Z), .N(N), .V(V), .S(alu_completa_t_1_s));
  Seven_Seg_Hex seven_seg_hex_3 (.d(b_2[7:4]), .dp(notconnected_2_out));
  not not_1 (not_1_out, clk);
  Seven_Seg_Hex seven_seg_hex_4 (.d(b_2[3:0]), .dp(notconnected_2_out));
  // NotConnected on notconnected_2_out
  _3a_reg_salida_restringida_8bits _3a_reg_salida_restringida_8bits_3 (
    .clk(not_1_out), .IN_8(alu_completa_t_1_s), .en_o(en_out), .W(1'b1), .out_d(S), .out(S_debug));
  Seven_Seg_Hex seven_seg_hex_5 (.d(S[7:4]), .dp(notconnected_3_out));
  Seven_Seg_Hex seven_seg_hex_6 (.d(S[3:0]), .dp(notconnected_3_out));
  // NotConnected on notconnected_3_out

  // Notes on the sheet:
  //   3b) ALU con registros de entrada y salida - 8 bits
endmodule
