// Digital circuit 3c_ALU_con_registros.dig as structural Verilog
module _3c_ALU_con_registros (
  input  clk,
  input  W0,
  input  W1,
  input  w_ALU_A,
  input  w_ALU_B,
  input  [2:0] OP,
  input  en_out_ALU,
  input  en_out_0,
  input  en_out_1,
  input  W2,
  input  en_out_2,
  input  W3,
  input  en_out_3,
  input  [7:0] Force_input,
  input  en_force_input,
  output [7:0] REG0,
  output [7:0] REG1,
  output C,
  output Z,
  output N,
  output V,
  output [7:0] REG2,
  output [7:0] REG3
);

  wire notconnected_1_out, notconnected_2_out, notconnected_3_out, notconnected_4_out, notconnected_5_out,
       notconnected_6_out, notconnected_7_out, notconnected_8_out, notconnected_9_out, notconnected_10_out,
       notconnected_11_out, notconnected_12_out, notconnected_13_out, notconnected_14_out,
       notconnected_15_out, notconnected_16_out, notconnected_17_out, notconnected_18_out;
  wire [3:0] _3a_reg_salida_restringida_8bits_1_out, _3a_reg_salida_restringida_8bits_1_out_2,
       _3b_alu_registros_4bits_1_b_2, _3b_alu_registros_4bits_1_b_2_2, _3b_alu_registros_4bits_1_s,
       _3b_alu_registros_4bits_1_s_2, driver_1_out, driver_1_out_2;
  wire [7:0] _3b_alu_registros_4bits_1_a_2;

  assign {driver_1_out_2, driver_1_out} = en_force_input ? Force_input : 8'bz;  // Driver driver_1
  _3a_reg_salida_restringida_8bits _3a_reg_salida_restringida_8bits_1 (
    .clk(clk), .IN_8({driver_1_out_2, driver_1_out}), .en_o(en_out_0), .W(W0), .out_d(REG0),
    .out({_3a_reg_salida_restringida_8bits_1_out_2, _3a_reg_salida_restringida_8bits_1_out}));
  _3a_reg_salida_restringida_8bits _3a_reg_salida_restringida_8bits_2 (
    .clk(clk), .IN_8({driver_1_out_2, driver_1_out}), .en_o(en_out_1), .W(W1), .out_d(REG1),
    .out({_3a_reg_salida_restringida_8bits_1_out_2, _3a_reg_salida_restringida_8bits_1_out}));
  _3a_reg_salida_restringida_8bits _3a_reg_salida_restringida_8bits_3 (
    .clk(clk), .IN_8({driver_1_out_2, driver_1_out}), .en_o(en_out_2), .W(W2), .out_d(REG2),
    .out({_3a_reg_salida_restringida_8bits_1_out_2, _3a_reg_salida_restringida_8bits_1_out}));
  _3a_reg_salida_restringida_8bits _3a_reg_salida_restringida_8bits_4 (
    .clk(clk), .IN_8({driver_1_out_2, driver_1_out}), .en_o(en_out_3), .W(W3), .out_d(REG3),
    .out({_3a_reg_salida_restringida_8bits_1_out_2, _3a_reg_salida_restringida_8bits_1_out}));
  Seven_Seg_Hex seven_seg_hex_1 (.d(REG0[7:4]), .dp(notconnected_1_out));
  // NotConnected on notconnected_1_out
  Seven_Seg_Hex seven_seg_hex_2 (.d(REG1[7:4]), .dp(notconnected_3_out));
  Seven_Seg_Hex seven_seg_hex_3 (.d(REG2[7:4]), .dp(notconnected_4_out));
  Seven_Seg_Hex seven_seg_hex_4 (.d(REG3[7:4]), .dp(notconnected_5_out));
  Seven_Seg_Hex seven_seg_hex_5 (.d(REG0[3:0]), .dp(notconnected_2_out));
  // NotConnected on notconnected_2_out
  Seven_Seg_Hex seven_seg_hex_6 (.d(REG1[3:0]), .dp(notconnected_6_out));
  // NotConnected on notconnected_3_out
  Seven_Seg_Hex seven_seg_hex_7 (.d(REG2[3:0]), .dp(notconnected_7_out));
  // NotConnected on notconnected_4_out
  Seven_Seg_Hex seven_seg_hex_8 (.d(REG3[3:0]), .dp(notconnected_8_out));
  // NotConnected on notconnected_5_out
  // NotConnected on notconnected_6_out
  // NotConnected on notconnected_7_out
  // NotConnected on notconnected_8_out
  Seven_Seg_Hex seven_seg_hex_9 (.d(_3a_reg_salida_restringida_8bits_1_out_2), .dp(notconnected_9_out));
  // NotConnected on notconnected_9_out
  Seven_Seg_Hex seven_seg_hex_10 (.d(_3a_reg_salida_restringida_8bits_1_out), .dp(notconnected_10_out));
  // NotConnected on notconnected_10_out
  _3b_ALU_registros_4bits _3b_alu_registros_4bits_1 (
    .clk(clk), .A({_3a_reg_salida_restringida_8bits_1_out_2, _3a_reg_salida_restringida_8bits_1_out}),
    .B({_3a_reg_salida_restringida_8bits_1_out_2, _3a_reg_salida_restringida_8bits_1_out}),
    .Write_A(w_ALU_A), .Write_B(w_ALU_B), .OP(OP), .en_out(en_out_ALU), .a_2(_3b_alu_registros_4bits_1_a_2),
    .b_2({_3b_alu_registros_4bits_1_b_2_2, _3b_alu_registros_4bits_1_b_2}),
    .S_debug({driver_1_out_2, driver_1_out}),
    .S({_3b_alu_registros_4bits_1_s_2, _3b_alu_registros_4bits_1_s}), .C(C), .Z(Z), .N(N), .V(V));
  Seven_Seg_Hex seven_seg_hex_11 (.d(driver_1_out_2), .dp(notconnected_11_out));
  Seven_Seg_Hex seven_seg_hex_12 (.d(_3b_alu_registros_4bits_1_a_2[7:4]), .dp(notconnected_12_out));
  Seven_Seg_Hex seven_seg_hex_13 (.d(driver_1_out), .dp(notconnected_13_out));
  // NotConnected on notconnected_11_out
  Seven_Seg_Hex seven_seg_hex_14 (.d(_3b_alu_registros_4bits_1_a_2[3:0]), .dp(notconnected_14_out));
  // NotConnected on notconnected_12_out
  // NotConnected on notconnected_13_out
  // NotConnected on notconnected_14_out
  Seven_Seg_Hex seven_seg_hex_15 (.d(_3b_alu_registros_4bits_1_b_2_2), .dp(notconnected_15_out));
  Seven_Seg_Hex seven_seg_hex_16 (.d(_3b_alu_registros_4bits_1_b_2), .dp(notconnected_16_out));
  // NotConnected on notconnected_15_out
  // NotConnected on notconnected_16_out
  Seven_Seg_Hex seven_seg_hex_17 (.d(_3b_alu_registros_4bits_1_s_2), .dp(notconnected_17_out));
  // NotConnected on notconnected_17_out
  Seven_Seg_Hex seven_seg_hex_18 (.d(_3b_alu_registros_4bits_1_s), .dp(notconnected_18_out));
  // NotConnected on notconnected_18_out

  // Notes on the sheet:
  //   3c) Secuencia de operación ALU con registros y buses - 8 bits
  //   OP
  //   0 0 0
  //   0 0 1
  //   0 1 0
  //   0 1 1
  //   1 0 0
  //   BUS 1
  //   ALU
  //   A  + B
  //   A  - B
  //   A  and B
  //   A  or B
  //   A x B
  //   BUS 2
  //   OP
  //   =
endmodule
