// Digital circuit Multiplicacion.dig as structural Verilog
module Multiplicacion (
  input  [7:0] a,
  input  [7:0] b,
  output [7:0] R,
  output O
);

  wire notconnected_1_out, notconnected_2_out;
  wire [3:0] mul_1_mul_2;
  wire [11:8] mul_1_mul;

  Seven_Seg_Hex seven_seg_hex_1 (.d(mul_1_mul_2), .dp(notconnected_1_out));
  Mul #(.Bits(8)) mul_1 (.a(a), .b(b), .mul({mul_1_mul_2, mul_1_mul, R}));
  Seven_Seg_Hex seven_seg_hex_2 (.d(R[7:4]), .dp(notconnected_2_out));
  Seven_Seg_Hex seven_seg_hex_3 (.d(mul_1_mul), .dp(notconnected_1_out));
  Seven_Seg_Hex seven_seg_hex_4 (.d(R[3:0]), .dp(notconnected_2_out));
  // NotConnected on notconnected_1_out
  // NotConnected on notconnected_2_out
  or or_1 (O, mul_1_mul[8], mul_1_mul[9], mul_1_mul[10], mul_1_mul[11], mul_1_mul_2[0], mul_1_mul_2[1], mul_1_mul_2[2], mul_1_mul_2[3]);
endmodule
