// Digital circuit complementadorA2_t.dig as structural Verilog
module complementadorA2_t (
  input  [7:0] B_2,
  input  Neg,
  output [7:0] B
);

  wire [7:0] not_1_out, sum_8bit_t_1_s;

  assign not_1_out = ~B_2;  // Not not_1, 8 bits wide
  sum_8bit_t sum_8bit_t_1 (.A(not_1_out), .B({8{1'b0}}), .Cin(1'b1), .S(sum_8bit_t_1_s));  // open: Cout
  Multiplexer #(.Bits(8)) multiplexer_1 (.sel(Neg), .in_0(B_2), .in_1(sum_8bit_t_1_s), .out(B));
endmodule
