// Digital circuit flag_cero_t.dig as structural Verilog
module flag_cero_t (
  input  [7:0] S,
  output Z
);

  wire or_1_out, or_2_out, or_3_out, or_4_out, or_5_out, or_6_out;

  or or_1 (or_1_out, S[0], S[1]);
  or or_2 (or_2_out, S[2], S[3]);
  or or_3 (or_3_out, S[4], S[5]);
  or or_4 (or_4_out, S[6], S[7]);
  or or_5 (or_5_out, or_1_out, or_2_out);
  or or_6 (or_6_out, or_3_out, or_4_out);
  nor nor_1 (Z, or_5_out, or_6_out);
endmodule
