// Digital circuit flag_overflow_t.dig as structural Verilog
module flag_overflow_t (
  input  a3,
  input  b3,
  input  s3,
  output V
);

  wire not_1_out, xor_1_out, xor_2_out;

  xor xor_1 (xor_1_out, a3, b3);
  xor xor_2 (xor_2_out, a3, s3);
  not not_1 (not_1_out, xor_1_out);
  and and_1 (V, not_1_out, xor_2_out);
endmodule
