// Digital circuit sum_8bit_t.dig as structural Verilog
module sum_8bit_t (
  input  [7:0] A,
  input  [7:0] B,
  input  Cin,
  output [7:0] S,
  output Cout
);

  wire sum_1bit_t_1_cout, sum_1bit_t_2_cout, sum_1bit_t_3_cout, sum_1bit_t_4_cout, sum_1bit_t_5_cout,
       sum_1bit_t_6_cout, sum_1bit_t_7_cout;

  sum_1bit_t sum_1bit_t_1 (.A(A[0]), .B(B[0]), .Cin(Cin), .S(S[0]), .Cout(sum_1bit_t_1_cout));
  sum_1bit_t sum_1bit_t_2 (.A(A[1]), .B(B[1]), .Cin(sum_1bit_t_1_cout), .S(S[1]), .Cout(sum_1bit_t_2_cout));
  sum_1bit_t sum_1bit_t_3 (.A(A[2]), .B(B[2]), .Cin(sum_1bit_t_2_cout), .S(S[2]), .Cout(sum_1bit_t_3_cout));
  sum_1bit_t sum_1bit_t_4 (.A(A[3]), .B(B[3]), .Cin(sum_1bit_t_3_cout), .S(S[3]), .Cout(sum_1bit_t_4_cout));
  sum_1bit_t sum_1bit_t_5 (.A(A[4]), .B(B[4]), .Cin(sum_1bit_t_4_cout), .S(S[4]), .Cout(sum_1bit_t_5_cout));
  sum_1bit_t sum_1bit_t_6 (.A(A[5]), .B(B[5]), .Cin(sum_1bit_t_5_cout), .S(S[5]), .Cout(sum_1bit_t_6_cout));
  sum_1bit_t sum_1bit_t_7 (.A(A[6]), .B(B[6]), .Cin(sum_1bit_t_6_cout), .S(S[6]), .Cout(sum_1bit_t_7_cout));
  sum_1bit_t sum_1bit_t_8 (.A(A[7]), .B(B[7]), .Cin(sum_1bit_t_7_cout), .S(S[7]), .Cout(Cout));
  Seven_Seg_Hex seven_seg_hex_1 (.d(S[7:4]), .dp(Cout));
  Seven_Seg_Hex seven_seg_hex_2 (.d(S[3:0]), .dp(Cout));
endmodule
